# Fritzing sketch ex02 (saved by Fritzing 0.9.3b)
breadboards: 1

parts:
  元件1 = Arduino Nano (Rev3.0)
  R1 = Resistor [tolerance=±5% resistance=470 package=THT]
  LED1 = LED - 5mm [color="Red (633nm)" package="5 mm [THT]"]
  R2 = Photocell (LDR) [package=THT]
  R3 = Temperature Sensor (Thermistor) [thermistor_type=NTC package=THT]
  R4 = Resistor [tolerance=±5% resistance=10k package=THT]
  R5 = Resistor [tolerance=±5% resistance=10k package=THT]

nets:
  N1: 元件1.GND, R4.Pin_0, R5.Pin_0
  N2: 元件1.D3, R1.Pin_0
  N3: 元件1.5V, 元件1.A1, 元件1.A0, R1.Pin_1, LED1.cathode, LED1.anode, R2.pin_0, R2.pin_1, R3.pin_0, R3.pin_1, R4.Pin_1, R5.Pin_1
